# Fritzing sketch layout_v0 (saved by Fritzing 0.9.1b)

parts:
  Part1 = Arduino Nano (Rev3.0)
  EchoLeft = SRF05 Ultrasonic Rangefinder
  EchoMiddle = SRF05 Ultrasonic Rangefinder
  EchoRight = SRF05 Ultrasonic Rangefinder
  Part5 = Triple Axis Magnetometer - HMC5883 Breakout
  MotorRight = DC Motor with two-phase hall-encoder [part_number=JBG37-520]
  MotorLeft = DC Motor with two-phase hall-encoder [part_number=JBG37-520]
  S1 = H-Bridge with L298N
  J1 = female pin header, 2 pins [form="♀ (female)"]
  BAT1 = 18650 battery holder [package=battery-18650-kit]

nets:
  N1: Part1.A5, Part5.SCL
  N2: Part1.A4, Part5.SDA
  VCC: EchoLeft.VCC, EchoMiddle.VCC, EchoRight.VCC, Part5.VCC, S1.5V, J1.pin1
  GND: EchoLeft.GND, EchoMiddle.GND, EchoRight.GND, Part5.GND, S1.GND, J1.pin2, BAT1.-
  N3: MotorRight.pin2, S1.M1-01
  N4: MotorLeft.pin1, S1.M2-01
  N5: MotorLeft.pin2, S1.M2-02
  N6: S1.12V, BAT1.+

custom parts:
  H-Bridge with L298N: h-bridge
  18650 battery holder: 18650 Battery Holder
